# Fritzing sketch v2.0 (saved by Fritzing 0.9.3b)
circuit board: 21cm x 29.7cm
breadboards: 1

parts:
  Czujnik_temperatury_i_wilgotności_DHT22_(AM2302) = female pin header, 3 pins [form="♀ (female)"]
  BUZZER = Buzzer 12mm [package=buzzer-12mm-ns]
  Nawilzacz = Resistor [tolerance=±5% resistance=220 package=THT]
  R1 = Resistor [tolerance=±5% resistance=68 package=THT]
  C1 = Electrolytic Capacitor [capacitance=1µF package="100 mil [THT, electrolytic]"]
  C2 = Ceramic Capacitor [capacitance=100nF package="100 mil [THT, multilayer]"]
  I2C = Resistor [tolerance=±5% resistance=10k package=THT]
  I2C1 = Resistor [tolerance=±5% resistance=10k package=THT]
  RST = Resistor [tolerance=±5% resistance=10k package=THT]
  Rezystor_(Czujnik_DS18B20) = Resistor [tolerance=±5% resistance=4.7k package=THT]
  R2 = Resistor [tolerance=±5% resistance=220 package=THT]
  LED_White_(100mA) = LED - 5mm [color="Red (633nm)" package="5 mm [THT]"]
  R3 = Resistor [tolerance=±5% resistance=220 package=THT]
  LED_RED_(100mA) = LED - 5mm [color="Red (633nm)" package="5 mm [THT]"]
  1_2_3_4 = female pin header, 5 pins [form="♀ (female)"]
  R4 = Resistor [tolerance=±5% resistance=10k package=THT]
  R5 = Resistor [tolerance=±5% resistance=10k package=THT]
  R6 = Resistor [tolerance=±5% resistance=10k package=THT]
  R7 = Resistor [tolerance=±5% resistance=10k package=THT]
  C3 = Ceramic Capacitor [capacitance=10nF package="100 mil [THT, multilayer]"]
  C4 = Ceramic Capacitor [capacitance=10nF package="100 mil [THT, multilayer]"]
  C5 = Ceramic Capacitor [capacitance=10nF package="100 mil [THT, multilayer]"]
  C6 = Ceramic Capacitor [capacitance=10nF package="100 mil [THT, multilayer]"]
  R8 = Resistor [tolerance=±5% resistance=68 package=THT]
  R9 = Resistor [tolerance=±5% resistance=68 package=THT]
  Dodatkowe_oswietlenie_1_(5V) = LED - 5mm [color="Red (633nm)" package="5 mm [THT]"]
  C7 = Ceramic Capacitor [capacitance=100nF package="100 mil [THT, multilayer]"]
  C9 = Ceramic Capacitor [capacitance=100nF package="100 mil [THT, multilayer]"]
  Dławik = Resistor [tolerance=±5% resistance=220 package=THT]
  C10 = Ceramic Capacitor [capacitance=100nF package="100 mil [THT, multilayer]"]
  Nokia_5110 = female pin header, 8 pins [form="♀ (female)"]
  Input_12V = double row female pin header, 2 pins [form="♀ (female)"]
  Stabilizator_3_3V = Voltage Regulator LM1117 [package=sot223]
  J4 = female pin header, 1 pin [form="♀ (female)"]
  J5 = female pin header, 1 pin [form="♀ (female)"]
  J6 = female pin header, 1 pin [form="♀ (female)"]
  J7 = female pin header, 1 pin [form="♀ (female)"]
  IC1 = MICROCONTROLLER [package=dil28-3-simon-kit]
  C11 = Ceramic Capacitor [capacitance=100nF package="100 mil [THT, multilayer]"]
  J2 = female pin header, 4 pins [form="♀ (female)"]
  Zegar_czasu_rzeczywistego = Real Time Clock Module - DS1307 RTC Breakout Board
  Czujnik_temperatury_DS18B20 = female pin header, 3 pins [form="♀ (female)"]
  Stabilizator_5V = Voltage Regulator - 5V [package="TO220 [THT]"]
  BC639_(Sterowanie_RED_12V) = NPN-Transistor [package="TO92 [THT]"]
  BC639_(Sterowanie_White_12V) = NPN-Transistor [package="TO92 [THT]"]
  BC639_(Sterowanie_nawilrzaczem) = NPN-Transistor [package="TO92 [THT]"]
  BC546B_(Sterowanie_podswietleniem_wyswietlacza) = NPN-Transistor [package="TO92 [THT]"]
  BC546B_(Sterowanie_dodatkowym_oświetleniem_1) = NPN-Transistor [package="TO92 [THT]"]

nets:
  5V: Czujnik_temperatury_i_wilgotności_DHT22_(AM2302).pin1, Nawilzacz.Pin_1, I2C.Pin_0, I2C1.Pin_0, RST.Pin_0, Rezystor_(Czujnik_DS18B20).Pin_0, R4.Pin_1, R5.Pin_1, R6.Pin_1, R7.Pin_1, Dodatkowe_oswietlenie_1_(5V).anode, C9.1, Dławik.Pin_0, C10.1, Stabilizator_3_3V.IN, Zegar_czasu_rzeczywistego.VCC, Czujnik_temperatury_DS18B20.pin1, Stabilizator_5V.output_voltage
  GND: Czujnik_temperatury_i_wilgotności_DHT22_(AM2302).pin2, BUZZER.2, C1.-, 1_2_3_4.pin1, C3.0, C4.0, C5.0, C6.0, C7.0, C9.0, C10.0, Nokia_5110.pin8, Input_12V.pin1, Stabilizator_3_3V.ADJ, IC1.GND, C11.0, Zegar_czasu_rzeczywistego.GND, Czujnik_temperatury_DS18B20.pin3, Stabilizator_5V.GND, BC639_(Sterowanie_RED_12V).E, BC639_(Sterowanie_White_12V).E, BC639_(Sterowanie_nawilrzaczem).E, BC546B_(Sterowanie_podswietleniem_wyswietlacza).E, BC546B_(Sterowanie_dodatkowym_oświetleniem_1).E
  N1: Czujnik_temperatury_i_wilgotności_DHT22_(AM2302).pin3, IC1.PB2(SS_OC1B)
  N2: BUZZER.1, IC1.PB6(XTAL1_TOSC1)
  N3: Nawilzacz.Pin_0, BC639_(Sterowanie_nawilrzaczem).C
  N4: R1.Pin_0, BC639_(Sterowanie_nawilrzaczem).B
  N5: R1.Pin_1, IC1.PB0(ICP)
  N6: C1.+, C2.0, Dławik.Pin_1, IC1.VCC
  N7: C2.1, IC1.AGND
  N8: I2C.Pin_1, IC1.PC4(ADC4_SDA), Zegar_czasu_rzeczywistego.SDA
  N9: I2C1.Pin_1, IC1.PC5(ADC5_SCL), Zegar_czasu_rzeczywistego.SCL
  N10: RST.Pin_1, IC1.PC6(_RESET), J2.pin4
  N11: Rezystor_(Czujnik_DS18B20).Pin_1, IC1.PB1(OC1A), Czujnik_temperatury_DS18B20.pin2
  N12: R2.Pin_0, BC639_(Sterowanie_RED_12V).B
  N13: R2.Pin_1, IC1.PD0(RXD)
  N14: LED_White_(100mA).cathode, BC639_(Sterowanie_RED_12V).C
  12V: LED_White_(100mA).anode, LED_RED_(100mA).anode, C7.1, Input_12V.pin2, Stabilizator_5V.input_voltage
  N15: R3.Pin_0, BC639_(Sterowanie_White_12V).B
  N16: R3.Pin_1, IC1.PC3(ADC3)
  N17: LED_RED_(100mA).cathode, BC639_(Sterowanie_White_12V).C
  N18: 1_2_3_4.pin2, R7.Pin_0, C6.1
  N19: 1_2_3_4.pin3, R6.Pin_0, C5.1, IC1.PD2(INT0)
  N20: 1_2_3_4.pin4, R5.Pin_0, C4.1, IC1.PC1(ADC1)
  N21: 1_2_3_4.pin5, R4.Pin_0, C3.1, IC1.PD3(INT1)
  N22: R8.Pin_0, BC546B_(Sterowanie_podswietleniem_wyswietlacza).B
  N23: R8.Pin_1, IC1.PB7(XTAL2_TOSC2)
  N24: R9.Pin_0, BC546B_(Sterowanie_dodatkowym_oświetleniem_1).B
  N25: R9.Pin_1, IC1.PC0(ADC0)
  N26: Dodatkowe_oswietlenie_1_(5V).cathode, BC546B_(Sterowanie_dodatkowym_oświetleniem_1).C
  N27: Nokia_5110.pin1, IC1.PD1(TXD)
  N28: Nokia_5110.pin2, IC1.PD4(XCK_T0)
  N29: Nokia_5110.pin3, IC1.PD5(T1)
  N30: Nokia_5110.pin4, IC1.PD6(AIN0)
  N31: Nokia_5110.pin5, IC1.PD7(AIN1)
  N32: Nokia_5110.pin6, Stabilizator_3_3V.OUT, C11.1
  N33: Nokia_5110.pin7, BC546B_(Sterowanie_podswietleniem_wyswietlacza).C
  N34: J4.pin1, J5.pin1, J6.pin1, J7.pin1
  N35: IC1.PB3(MOSI_OC2), J2.pin1
  N36: IC1.PB4(MISO), J2.pin2
  N37: IC1.PB5(SCK), J2.pin3

notes:
  2019
  By_Olek
  Ver
  12V
  Input
  1.1
  +
  -

custom parts:
  Real Time Clock Module - DS1307 RTC Breakout Board: This a custom designed module for the DS1307 Real Time Clock. The module comes fully assembled and pre-programmed with the current time (ok, so it's our current time - MST). The included Lithium coin cell battery (CR1225 41mAh) will run the module for a minimum of 9 years (17 years typical) without external 5V power. The DS1307 is accessed via the I2C protocol. We've written a test-bed to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
